# Fritzing sketch luces (saved by Fritzing 0.9.3b)

parts:
  S1 = Pushbutton [package=THT]
  Raspberry_Pi_1 = Raspberry Pi 3 [part_number=RPI-3-V1.2]
  S2 = Pushbutton [package=THT]
  S3 = Pushbutton [package=THT]
  LED1 = LED - 5mm [color="Red (633nm)" package="5 mm [THT]"]
  LED2 = LED - 5mm [color="Red (633nm)" package="5 mm [THT]"]
  LED3 = LED - 5mm [color="Red (633nm)" package="5 mm [THT]"]
  LED4 = LED - 5mm [color="Red (633nm)" package="5 mm [THT]"]
  LED5 = LED - 5mm [color="Red (633nm)" package="5 mm [THT]"]

nets:
  N1: S1.leg0, Raspberry_Pi_1.GPIO18
  N2: S1.leg1, Raspberry_Pi_1.5V, S2.leg1, S3.leg1
  N3: Raspberry_Pi_1.GPIO2, LED1.anode
  N4: Raspberry_Pi_1.GPIO3, LED2.anode
  N5: Raspberry_Pi_1.GPIO4, LED3.anode
  N6: Raspberry_Pi_1.GPIO17, LED4.anode
  N7: Raspberry_Pi_1.GPIO27, LED5.anode
  N8: Raspberry_Pi_1.GPIO15, S2.leg0
  N9: Raspberry_Pi_1.GPIO14, S3.leg0
  N10: Raspberry_Pi_1.GND, LED1.cathode, LED2.cathode, LED3.cathode, LED4.cathode, LED5.cathode
